# Fritzing sketch ESP32_Wiring_0.1 (saved by Fritzing 0.9.10b)
circuit board: 7.22179cm x 5.59933cm
breadboards: 1

parts:
  ESP32-CAM = ESP32 - CAM
  NEOPIXEL1 = Neopixel Strip -- Black (60/m) [part_number=1461]
  C1 = Electrolytic Capacitor [capacitance=1mF voltage=16V package="100 mil [THT, electrolytic]"]
  Boot = Momentary Switch [package=ksa_sealed_tac_switch]
  Level_Shifter = Adafruit 4-channel I2C-safe Bi-directional Logic Level Converter [part_number="Adafruit #757"]
  USBTTL1 = USB TTL Serial Cable
  AW9523_GPIO_Expansion = Adafruit AW9523 [part_number="Adafruit #4886"]
  USB_Power = Adafruit Micro USB Breakout [part_number="Adafruit #1833"]

nets:
  5V: ESP32-CAM.5V, NEOPIXEL1.+5V, C1.+, Level_Shifter.HV, USBTTL1.5V, AW9523_GPIO_Expansion.VCC, USB_Power.VBUS
  GND: ESP32-CAM.GND, NEOPIXEL1.GND, C1.-, Boot.1, Level_Shifter.GND, USBTTL1.GND, AW9523_GPIO_Expansion.GND, USB_Power.GND
  N1: ESP32-CAM.IO13, Level_Shifter.A4
  N2: ESP32-CAM.IO14, AW9523_GPIO_Expansion.SDA
  N3: ESP32-CAM.IO2, AW9523_GPIO_Expansion.SCL
  N4: ESP32-CAM.VOT, USBTTL1.RX
  N5: ESP32-CAM.VOR, USBTTL1.TX
  N6: ESP32-CAM.IO0, Boot.3
  N7: ESP32-CAM.3V3, Level_Shifter.LV
  N8: NEOPIXEL1.DI, Level_Shifter.B4

custom parts:
  ESP32 - CAM: The ESP32-CAM has a very competitive small-size camera module that can operate independently as a minimum system with a footprint of only 27*40.5*4.5mm and a deep sleep current of up to 6mA.
  Neopixel Strip -- Black (60/m): Neopixel Strip, Black, 60 pixels per meter.
  Adafruit 4-channel I2C-safe Bi-directional Logic Level Converter: Because the Arduino (and Basic Stamp) are 5V devices, and most modern sensors, displays, flash cards and modes are 3.3V-only, many makers find that they need to perform level shifting/conversion to protect the 3.3V device from 5V. We do have some other handy level shifters in the shop, from the DIP 74LVC245 to the fancy bi-directional TXB0108. However, neither of these are happy to work with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
  Adafruit AW9523: Expand your project possibilities, with the Adafruit AW9523 GPIO Expander and LED Driver Breakout - a cute and powerful I2C expander with a lot of tricks up it's sleeve. GPIO expanders work like this: you have a board with some number of GPIO but not enough for your project - maybe you need more buttons or LEDs. You could upgrade to a board with massive number of GPIO like the Grand Central,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
  Adafruit Micro USB Breakout: Simple but effective - this breakout board has a USB Micro-B connector, with all 5 pins broken out. Great for pairing with a microcontroller with USB support, or adding USB 5V power to a project. We use a micro-AB connector with through-hole shielding pads for an excellent strong connection - it won't rip off by accident! Comes with one fully assembled and tested micro B breakout PCB and a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
